# Fritzing sketch oximeter_thermometer (saved by Fritzing 0.9.3b)
breadboards: 2

parts:
  Onderdeel1 = Arduino Uno (Rev3)
  LED1 = smd LED [color="Infrared (850nm)" package="0805 [SMD]"]
  LED2 = smd LED [color="Red (633nm)" package="0805 [SMD]"]
  R1 = Resistor [tolerance=±5% resistance=330 package="0603 [SMD]"]
  LCD1 = LCD screen
  R4 = Resistor [tolerance=±5% resistance=330 package="0603 [SMD]"]
  R3 = Resistor [tolerance=±5% resistance=10k package="0603 [SMD]"]
  R5 = Resistor [tolerance=±5% resistance=4.7k package=THT]
  R7 = Resistor [tolerance=±5% resistance=220 package=THT]
  R9 = Rotary Potentiometer (Small) [maximum_resistance=50kΩ package=THT]
  P1 = S1133 Si Photodiode [package="8mm Ceramic [THT]"]
  R10 = Resistor [tolerance=±5% resistance=330 package=THT]
  LED3 = LED - 3mm [color="White (4500K)" package="3 mm [THT]"]
  DS1 = DS18B20 1-Wire Temperature Sensor [part_number=DS18B20]
  Componente1 = Bluetooth HC-05 Macho

nets:
  N1: Onderdeel1.A0, R3.Pin_1, P1.anode
  N2: Onderdeel1.D8, R1.Pin_1
  N3: Onderdeel1.D9_PWM, R4.Pin_1
  N4: Onderdeel1.D10_PWM/SS, R5.Pin_1, DS1.DQ
  N5: Onderdeel1.D13/SCK, R10.Pin_1
  GND: Onderdeel1.GND, LED1.cathode, LED2.cathode, LCD1.VSS, LCD1.R/W, LCD1.LED-, R9.leg2, P1.cathode, LED3.cathode, DS1.GND, Componente1.GND
  N6: Onderdeel1.D0/RX, Componente1.TXD
  N7: Onderdeel1.D1/TX, Componente1.RXD
  N8: Onderdeel1.D2, LCD1.DB7
  N9: Onderdeel1.D3_PWM, LCD1.DB6
  N10: Onderdeel1.D4, LCD1.DB5
  N11: Onderdeel1.D5_PWM, LCD1.DB4
  N12: Onderdeel1.D6_PWM, LCD1.E
  N13: Onderdeel1.D7, LCD1.RS
  VDD: Onderdeel1.5V, LCD1.VDD, R3.Pin_0, R5.Pin_0, R7.Pin_0, R9.leg1, DS1.VDD, Componente1.VCC
  N14: LED1.anode, R1.Pin_0
  N15: LED2.anode, R4.Pin_0
  N16: LCD1.V0, R9.wiper
  N17: LCD1.LED+, R7.Pin_1
  N18: R10.Pin_0, LED3.anode

notes:
  In order to simulatethe ky-001 and ky-039electronic modules, Icreated thisprotoboard

// code stored in the sketch: AnalogReadSerial2LCD_LED.ino
#include <Wire.h>
#include <LiquidCrystal_I2C.h>

LiquidCrystal_I2C lcd(0x27, 16, 2);   // adress and format LCD

const int analogInPin = A0;           // Analog input pin that the potentiometer is attached to
const int analogOutPin = 9;           // Analog output pin that the LED is attached to

int sensorValue = 0;                  // value read from the pot
int outputValue = 0;                  // value output to the PWM (analog out)

void setup() {
  lcd.init();                         // init LCD
  lcd.backlight();
  lcd.home();
  lcd.setCursor(5, 0);                // place static text
  lcd.print("ADC = ");
  lcd.setCursor(15, 0);
  lcd.print("V");
  lcd.setCursor(0, 1);
  lcd.print("LED : ");
  lcd.setCursor(12, 1);
  lcd.print("%");
  Serial.begin(9600);                 // optional serial monitor
}

void loop() {
  int sensorValue = analogRead(analogInPin);          // read analog A0 en store in sensorValue
  float voltValue = 5.0 / 1024.0 * sensorValue;       // calculate volt at analog A0 and store in voltValue
  float percentValue = sensorValue / 1024.0 * 100.0;  // calculate percentage analog A0 and store in percentValue
  outputValue = map(sensorValue, 0, 1023, 0, 255);    // map analog input to analog output and store in outputValue
  analogWrite(analogOutPin, outputValue);             // write outputValue to analogOutPin

  lcd.setCursor(0, 0);                                // set cursor at deserid position
  leadingZeros(sensorValue, 4);                       // print sensorvalue with number of leading-characters (0 or space as specified in function leadingZeros)
  lcd.setCursor(10, 0);                               // set cursor at deserid position
  lcd.print(voltValue);                               // print voltValue
  lcd.setCursor(6, 1);                                // set cursor at deserid position
  lcd.print(percentValue);                            // print percentValue

  Serial.print("sensor = " );                         // print the results to the serial monitor:
  Serial.print(sensorValue);
  Serial.print("\t output = ");
  Serial.print(outputValue);
  Serial.print("\t procent = ");
  Serial.println(percentValue);

  delay(1000);                                        // set delay
}

void leadingZeros( int value, int width) {            // display result with leading characters
  char valueStr[6];                                   // large enough to hold an int
  itoa (value, valueStr, 10);                         // itoa converts int to string
  int len = strlen(valueStr);                         // calculate length of valueStr
  if (len < width) {
    len = width - len;
    while (len--)
      lcd.print(' ');                                 // for leading zeros place '0' between (), for leading spaces place ' ' between ()
  }
  lcd.print(valueStr);
}

// code stored in the sketch: oximeter_thermometer.ino
//DISPLAY 16X2
#include <LiquidCrystal.h>

// a liquid crystal displays data
LiquidCrystal lcd (7, 6, 5, 4, 3, 2);


//BEAT SENSOR
#define maxperiod_siz 80 // max number of samples in a period
#define measures 10      // number of periods stored
#define samp_siz 4       // number of samples for average
#define rise_threshold 3 // number of rising measures to determine a peak

int T = 20;              // slot milliseconds to read a value from the sensor
const int sensorPin = A0; 
const int REDLed = 9;
const int IRLed = 8;
const int WHITELed = 13;

byte sym[3][8] =
{
 {
  B00000,
  B01010,
  B11111,
  B11111,
  B01110,
  B00100,
  B00000,
  B00000
},{
  B00000,
  B00000,
  B00000,
  B11000,
  B00100,
  B01000,
  B10000,
  B11100
},{
  B00000,
  B00100,
  B01010,
  B00010,
  B00100,
  B00100,
  B00000,
  B00100
}
};

//TEMP SENSOR
#include <OneWire.h>

int HighByte, LowByte, TReading, SignBit, Tc_100;  //needed values
float Whole = 0.0, Fract = 0.0;
 
// DS18S20 Temperature chip i/o
OneWire ds(10);  // on pin 10

void setup()
{
  Serial.begin(9600);
  Serial.flush();
  pinMode(sensorPin,INPUT);
  pinMode(REDLed,OUTPUT);
  pinMode(IRLed,OUTPUT);
  pinMode(WHITELed,OUTPUT);

  lcd.begin (16,2);   // set up the LCD's number of columns and rows:

  //Serial.println("SensandoSignosVitales"); // prints in monitor

  //lcd.setCursor(0,0);
  //lcd.print("Inic. Medicion");  //prints in lsc screen

  // turn off leds
  digitalWrite(REDLed,LOW);
  digitalWrite(IRLed,LOW);

  for(int i=0;i<8;i++) lcd.createChar(i, sym[i]);
  
}

void loop()
{
  bool finger_status = true;
  
  float readsIR[samp_siz], sumIR,lastIR, reader, start;
  float readsRED[samp_siz], sumRED,lastRED;


  int period, samples;
  period=0; samples=0;
  int samplesCounter = 0;
  float readsIRMM[maxperiod_siz],readsREDMM[maxperiod_siz];
  int ptrMM =0;
  for (int i = 0; i < maxperiod_siz; i++) { readsIRMM[i] = 0;readsREDMM[i]=0;}
  float IRmax=0;
  float IRmin=0;
  float REDmax=0;
  float REDmin=0;
  double R=0;

  float measuresR[measures];
  int measuresPeriods[measures];
  int m = 0;
  for (int i = 0; i < measures; i++) { measuresPeriods[i]=0; measuresR[i]=0; }
   
  int ptr;

  float beforeIR;

  bool rising;
  int rise_count;
  int n;
  long int last_beat;
  for (int i = 0; i < samp_siz; i++) { readsIR[i] = 0; readsRED[i]=0; }
  sumIR = 0; sumRED=0; 
  ptr = 0; 
    
  digitalWrite(WHITELed,LOW);

  while(1)
  {
     
    //
    // turn on IR LED
    digitalWrite(REDLed,LOW);
    digitalWrite(IRLed,HIGH);
    
    // calculate an average of the sensor
    // during a 20 ms (T) period (this will eliminate
    // the 50 Hz noise caused by electric light
    n = 0;
    start = millis();
    reader = 0.;
    
    do
    {
      reader += analogRead (sensorPin);
      n++;
    }
    while (millis() < start + T);
    
    reader /= n;  // we got an average
    // Add the newest measurement to an array
    // and subtract the oldest measurement from the array
    // to maintain a sum of last measurements
    sumIR -= readsIR[ptr];
    sumIR += reader;
    readsIR[ptr] = reader;
    lastIR = sumIR / samp_siz;


    
    //
    // TURN ON RED LED and do the same
    
    digitalWrite(REDLed,HIGH);
    digitalWrite(IRLed,LOW);

    n = 0;
    start = millis();
    reader = 0.;
    do
    {
      reader += analogRead (sensorPin);
      n++;
    }
    while (millis() < start + T);  
    
    reader /= n;  // we got an average
    // Add the newest measurement to an array
    // and subtract the oldest measurement from the array
    // to maintain a sum of last measurements
    sumRED -= readsRED[ptr];
    sumRED += reader;
    readsRED[ptr] = reader;
    lastRED = sumRED / samp_siz;


    //                                  
    // R CALCULATION
    // save all the samples of a period both for IR and for RED
    readsIRMM[ptrMM]=lastIR;
    readsREDMM[ptrMM]=lastRED;
    ptrMM++;
    ptrMM %= maxperiod_siz;
    samplesCounter++;
    //
    // if I've saved all the samples of a period, look to find
    // max and min values and calculate R parameter
    if(samplesCounter>=samples)
    {
      samplesCounter =0;
      IRmax = 0; IRmin=1023; REDmax = 0; REDmin=1023;
      for(int i=0;i<maxperiod_siz;i++)
      {
        if( readsIRMM[i]> IRmax) IRmax = readsIRMM[i];
        if( readsIRMM[i]>0 && readsIRMM[i]< IRmin ) IRmin = readsIRMM[i];
        readsIRMM[i] =0;
        if( readsREDMM[i]> REDmax) REDmax = readsREDMM[i];
        if( readsREDMM[i]>0 && readsREDMM[i]< REDmin ) REDmin = readsREDMM[i];
        readsREDMM[i] =0;
      }
      R =  ( (REDmax-REDmin) / REDmin) / ( (IRmax-IRmin) / IRmin ) ;
    }


    float avR = 0;
    int avBPM=0;

    if (finger_status==true)
    {
          
      // lastIR holds the average of the values in the array
      // check for a rising curve (= a heart beat)
      if (lastIR > beforeIR)
      {
        rise_count++;  // count the number of samples that are rising
        if (!rising && rise_count > rise_threshold)
        {
          // Ok, we have detected a rising curve, which implies a heartbeat.
          // Record the time since last beat, keep track of the 10 previous
          // peaks to get an average value.
          // The rising flag prevents us from detecting the same rise 
          // more than once. 
          rising = true;
      
          measuresR[m] = R;
          measuresPeriods[m] = millis() - last_beat;
          last_beat = millis();
          int period = 0;
          for(int i =0; i<measures; i++) period += measuresPeriods[i];
          
          // calculate average period and number of samples
          // to store to find min and max values
          period = period / measures;
          samples = period / (2*T);
            
          int avPeriod = 0;
          
          int c = 0;
          // c stores the number of good measures (not floating more than 10%),
          // in the last 10 peaks
          for(int i =1; i<measures; i++)
          {
            if ((measuresPeriods[i] <  measuresPeriods[i-1] * 1.1) && (measuresPeriods[i] >  measuresPeriods[i-1] / 1.1)) 
            {
              c++;
              avPeriod += measuresPeriods[i];
              avR += measuresR[i];
            }
          }
            
          m++;
          m %= measures;
                        
          //lcd.setCursor(9,0);
          //lcd.print("c= "+String(c)+"  ");
          
          
          // bpm and R shown are calculated as the
          // average of at least 5 good peaks
          avBPM = 60000 / ( avPeriod / c) ;
          avR = avR / c ;
          
          // if there are at last 5 measures 
          lcd.setCursor(9,1);
          if(c==0)
          {
            lcd.print("R=?.??");
            lcd.setCursor(0,0);
            lcd.print("bpm= - ");
            lcd.setCursor(0,1);
            lcd.print("SpO2= - ");
          }
          else
          {
            lcd.print("R=" + String(avR) + " ");
          }
            
          // if there are at least 5 good measures...
          if(c > 2)
          {
            digitalWrite(WHITELed,HIGH);
            // SATURTION IS A FUNCTION OF R (calibration)
            // Y = k*x + m
            // k and m are calculated with another oximeter
            int SpO2 = -19 * R + 102;
              
            lcd.setCursor(0,0);
            if(avBPM > 40 && avBPM <220)
            {
              lcd.print("         ");
              lcd.setCursor(0,0);
              lcd.print("bpm=" + String(avBPM));
            }
            else
            {
              lcd.setCursor(0,0);
              lcd.print("         ");
              lcd.setCursor(0,0);
              lcd.print("bpm= - ");
            }
    
            lcd.setCursor(0,1); 
            if(SpO2 > 70 && SpO2 <150) 
            {
              lcd.print("         ");
              lcd.setCursor(0,1); 
              lcd.print("SpO2=" + String(SpO2) + "%"); //else lcd.print("--% ");
            }
            else
            {
              lcd.setCursor(0,1);
              lcd.print("         ");
              lcd.setCursor(0,1);
              lcd.print("SpO2= - ");
            }
            digitalWrite(WHITELed,LOW);
            avR = (String(avR) == " NAN") ? 0.0 : avR;

            //sends the infomation to the python program
            //Serial.print(String(avBPM)+","+String(SpO2)+","+String(avR)+","+String(c)+"\n"); 
            Serial.print(float(avBPM));
            Serial.print(","); 
            Serial.print(float(SpO2));
            Serial.print(","); 
            Serial.print(float(avR));
            Serial.print(","); 
            Serial.println(float(Whole));                         
          }
        }
      }
      else
      {
        // Ok, the curve is falling
        rising = false;
        rise_count = 0;
        //lcd.setCursor(3,0);lcd.print(" ");
      }
      
      // to compare it with the new value and find peaks
      beforeIR = lastIR;
      
      termometro();//gets the temperature
      
    } // finger is inside
   
    
    // PLOT everything
    //Serial.print(lastIR);
    //Serial.print(",");
    //Serial.print(lastRED);
    //Serial.println();

    // handle the arrays      
    ptr++;
    ptr %= samp_siz;    
  } // loop while 1
}


void termometro()
{
  lcd.setCursor(8,0);
  lcd.print("tmp=");
     
  //For conversion of raw data to C
 
  byte i;
  byte present = 0;
  byte data[12];
  byte addr[8];
 
  if (!ds.search(addr))
  {
    //Serial.print("No more addresses.\n");
    ds.reset_search();
    return;
  }

  ds.reset();
  ds.select(addr);
  ds.write(0x44,1);
 
  present = ds.reset();
  ds.select(addr);    
  ds.write(0xBE);         // Read Scratchpad

  for ( i = 0; i < 9; i++)
  {           // 9 bytes are needed
    data[i] = ds.read();
  }
  
  //Conversion of raw data to C
  LowByte = data[0];
  HighByte = data[1];
  TReading = (HighByte << 8) + LowByte;
  SignBit = TReading & 0x8000;  // test most sig bit
  if (SignBit) // negative
  {
    TReading = (TReading ^ 0xffff) + 1; // 2's comp
  }
  Tc_100 = (6 * TReading) + TReading / 4;    // multiply by (100 * 0.0625) or 6.25
 
  Whole = Tc_100 / 100;  // separate off the whole and fractional portions
  Fract = Tc_100 % 10000;

  Whole += Fract;  //gets a single float value 
  Whole /= 100;
 
  //prints on Serial Monitor
  //Serial.print(Whole);
  //Serial.print("\n");

  //prints on lcd
  lcd.setCursor(12,0);
  lcd.print("    ");
  lcd.setCursor(12,0);
  lcd.print(Whole);
  //End conversion to C
}

// code stored in the sketch: plotter_and_data_saver_python.py.ino
#-----specifing libraries
import serial   # import Serial Library
import time     # import time library
import numpy    # Import numpy
import math     # importa math library
import matplotlib.pyplot as plt #import matplotlib library
from drawnow import *
import os       #in order to verify if a file is empty
from datetime import datetime   #in order to get the date and the time


now = datetime.now()    # datetime object containing current date and time


# Month abbreviation, day and year
#E.g. dec-12-02,22:12:08
dt = now.strftime("%b-%d-%Y,%H:%M:%S")


#--------crating a file
f = open('data.csv', 'a')     #opens the file just for making sure it exists
f.close()


if os.stat("data.csv").st_size == 0:    #if the file is empty it writes the headers
    f = open('data.csv', 'a')
    f.write("date,time,bpm,SpO2,R,Temp\n")
    #print("date,time,bpm,SpO2,R,Temp")
    f.close()


#--- variables (Serial data format  = heartBeat,oxigen,R,Temp)
#--- plot variables
oxygenPlot = []
heartBeatPlot = []
RPlot = []
tempPlot = []


arduinoData = serial.Serial('COM3', '9600') #Creating our serial object named arduinoData 9600 baudios
#arduinoData.flushInput()
plt.ion() #Tell matplotlib you want interactive mode to plot live data
cnt=0 


#--- functions
def makeFig(): #Create a function that makes our desired plot
    plt.ylim(40,240)                                #Set y min and max values
    plt.title('Pulsioxímetro, temperatura')                           #Plot the title
    plt.grid(True)                                  #Turn the grid on
    plt.ylabel('bpm and SpO2') 
    plt.xlabel('beats')                             #Set x and y labels
    plt.plot(heartBeatPlot, 'ro-', label='bpm')     #plot data ('xo-')
    plt.plot(oxygenPlot, 'bo-', label='SpO2')
    plt.legend(loc='upper left')                    #plot the legend
    plt2=plt.twinx()                                #Create a second y axis
    plt2.plot(tempPlot, 'go-', label='temp')
    plt.ylim(20,40)                         #Set limits of second y axis- adjust to readings you are getting
    plt2.set_ylabel('Temp (°C)')                #label second y axis
    #plt2.ticklabel_format(useOffset=False)        #Force matplotlib to NOT autoscale y axis
    plt2.legend(loc='upper right')                #plot the legend


# main 
while True: # While loop that loops forever
    while (arduinoData.inWaiting()==0): #Wait here until there is data
        pass #do nothing
    
    # format data
    arduinoString = arduinoData.readline() #read the line of text from the serial port
    dataArray = arduinoString.decode().split(',')   #Split it into an array called dataArray oxig 


    #--- save data
    vitalSigns =    {
        'heartBeatData' : str(int(float(dataArray[0]))),
        'oxygenData' : str(int(float(dataArray[1]))),
        'RData' : str(float(dataArray[2])),
        'tempData' : str(float(dataArray[3]))   }


    #--- build independent data
    #auxHeartBeatData.append(auxArduinoFloat)
    heartBeatPlot.append(float(vitalSigns['heartBeatData']))
    oxygenPlot.append(float(vitalSigns['oxygenData']))        #Build our aux array by appending data readings
    RPlot.append(float(vitalSigns['RData']))
    tempPlot.append(float(vitalSigns['tempData']))
    
    #--- call plot
    drawnow(makeFig)                       #Call drawnow to update our live graph
    plt.pause(.000001)                     #Pause Briefly. Important to keep drawnow from crashing (sec)
    cnt=cnt+1
    if(cnt>50):                        #If you have 50 or more points, delete the first one from the array
        heartBeatPlot.pop(0)                #This allows us to just see the last 50 data points
        oxygenPlot.pop(0)
        #RPlot.pop(0)
        tempPlot.pop(0)
    
    #---save in a csv file in the follow format:
        #date,time,bpm,SpO2,R,Temp
    now = datetime.now()    # datetime object containing current date and time


    # Month abbreviation, day and year
        #E.g. dec-12-02,22:12:08
    dt = now.strftime("%b-%d-%Y,%H:%M:%S")


    f = open('data.csv', 'a')
    f.write(dt + ',' + vitalSigns['heartBeatData'] + ','+ vitalSigns['oxygenData'] + ','+ vitalSigns['RData'] + ','+ vitalSigns['tempData'] + '\n')
    f.close()       #opens, writes and closes the file


    # print(dt, end=',')
    # for i in vitalSigns.values():
    #     if i == str(float(dataArray[3])):
    #         print(i)
    #     else:
    #         print(i, end=',')
