# Fritzing sketch oximeter-diy_oW9ZI5zQtJ (saved by Fritzing 0.9.3b)
breadboards: 2

parts:
  Onderdeel1 = Arduino Uno (Rev3)
  LED1 = smd LED [color="Infrared (850nm)" package="0805 [SMD]"]
  LED2 = smd LED [color="Red (633nm)" package="0805 [SMD]"]
  P1 = S1133 Si Photodiode [package="8mm Ceramic [THT]"]
  R1 = Resistor [tolerance=±5% resistance=330 package="0603 [SMD]"]
  LCD1 = LCD screen
  R4 = Resistor [tolerance=±5% resistance=330 package="0603 [SMD]"]
  R3 = Resistor [tolerance=±5% resistance=10k package="0603 [SMD]"]
  R5 = Resistor [tolerance=±5% resistance=4.7k package=THT]
  R7 = Resistor [tolerance=±5% resistance=220 package=THT]
  R9 = Rotary Potentiometer (Small) [maximum_resistance=50kΩ package=THT]
  LED3 = smd LED [color="Infrared (850nm)" package="0805 [SMD]"]
  R10 = Resistor [tolerance=±5% resistance=330 package="0603 [SMD]"]
  DS3 = DS18B20 1-Wire Temperature Sensor [part_number=DS18B20]

nets:
  N1: Onderdeel1.A0, P1.anode, R3.Pin_1
  N2: Onderdeel1.D8, R1.Pin_1
  N3: Onderdeel1.D9_PWM, R4.Pin_1
  N4: Onderdeel1.D10_PWM/SS, R5.Pin_1, DS3.DQ
  N5: Onderdeel1.D13/SCK, R10.Pin_1
  N6: Onderdeel1.D2, LCD1.DB7
  N7: Onderdeel1.D3_PWM, LCD1.DB6
  N8: Onderdeel1.D4, LCD1.DB5
  N9: Onderdeel1.D5_PWM, LCD1.DB4
  N10: Onderdeel1.D6_PWM, LCD1.E
  N11: Onderdeel1.D7, LCD1.RS
  VDD: Onderdeel1.5V, LCD1.VDD, R3.Pin_0, R5.Pin_0, R7.Pin_0, R9.leg1, DS3.VDD
  GND: Onderdeel1.GND, LED1.cathode, LED2.cathode, P1.cathode, LCD1.VSS, LCD1.R/W, LCD1.LED-, R9.leg2, LED3.cathode, DS3.GND
  N12: LED1.anode, R1.Pin_0
  N13: LED2.anode, R4.Pin_0
  N14: LCD1.V0, R9.wiper
  N15: LCD1.LED+, R7.Pin_1
  N16: LED3.anode, R10.Pin_0

notes:
  El LED1 is a IR LED

// code stored in the sketch: AnalogReadSerial2LCD_LED.ino
#include <Wire.h>
#include <LiquidCrystal_I2C.h>

LiquidCrystal_I2C lcd(0x27, 16, 2);   // adress and format LCD

const int analogInPin = A0;           // Analog input pin that the potentiometer is attached to
const int analogOutPin = 9;           // Analog output pin that the LED is attached to

int sensorValue = 0;                  // value read from the pot
int outputValue = 0;                  // value output to the PWM (analog out)

void setup() {
  lcd.init();                         // init LCD
  lcd.backlight();
  lcd.home();
  lcd.setCursor(5, 0);                // place static text
  lcd.print("ADC = ");
  lcd.setCursor(15, 0);
  lcd.print("V");
  lcd.setCursor(0, 1);
  lcd.print("LED : ");
  lcd.setCursor(12, 1);
  lcd.print("%");
  Serial.begin(9600);                 // optional serial monitor
}

void loop() {
  int sensorValue = analogRead(analogInPin);          // read analog A0 en store in sensorValue
  float voltValue = 5.0 / 1024.0 * sensorValue;       // calculate volt at analog A0 and store in voltValue
  float percentValue = sensorValue / 1024.0 * 100.0;  // calculate percentage analog A0 and store in percentValue
  outputValue = map(sensorValue, 0, 1023, 0, 255);    // map analog input to analog output and store in outputValue
  analogWrite(analogOutPin, outputValue);             // write outputValue to analogOutPin

  lcd.setCursor(0, 0);                                // set cursor at deserid position
  leadingZeros(sensorValue, 4);                       // print sensorvalue with number of leading-characters (0 or space as specified in function leadingZeros)
  lcd.setCursor(10, 0);                               // set cursor at deserid position
  lcd.print(voltValue);                               // print voltValue
  lcd.setCursor(6, 1);                                // set cursor at deserid position
  lcd.print(percentValue);                            // print percentValue

  Serial.print("sensor = " );                         // print the results to the serial monitor:
  Serial.print(sensorValue);
  Serial.print("\t output = ");
  Serial.print(outputValue);
  Serial.print("\t procent = ");
  Serial.println(percentValue);

  delay(1000);                                        // set delay
}

void leadingZeros( int value, int width) {            // display result with leading characters
  char valueStr[6];                                   // large enough to hold an int
  itoa (value, valueStr, 10);                         // itoa converts int to string
  int len = strlen(valueStr);                         // calculate length of valueStr
  if (len < width) {
    len = width - len;
    while (len--)
      lcd.print(' ');                                 // for leading zeros place '0' between (), for leading spaces place ' ' between ()
  }
  lcd.print(valueStr);
}

// code stored in the sketch: pulsioxiometro_con_lcd.ino
#include <LiquidCrystal.h>

#define maxperiod_siz 80 // max number of samples in a period
#define measures 10      // number of periods stored
#define samp_siz 4       // number of samples for average
#define rise_threshold 3 // number of rising measures to determine a peak
 
// a liquid crystal displays BPM 
LiquidCrystal lcd (7, 6, 5, 4, 3, 2);

int T = 20;              // slot milliseconds to read a value from the sensor
const int sensorPin = A0; 
const int REDLed = 9;
const int IRLed = 8;
const int WHITELed = 13;

byte sym[3][8] =
{
 {
  B00000,
  B01010,
  B11111,
  B11111,
  B01110,
  B00100,
  B00000,
  B00000
},{
  B00000,
  B00000,
  B00000,
  B11000,
  B00100,
  B01000,
  B10000,
  B11100
},{
  B00000,
  B00100,
  B01010,
  B00010,
  B00100,
  B00100,
  B00000,
  B00100
}
};

void setup()
{
  Serial.begin(9600);
  Serial.flush();
  pinMode(sensorPin,INPUT);
  pinMode(REDLed,OUTPUT);
  pinMode(IRLed,OUTPUT);
  pinMode(WHITELed,OUTPUT);

  lcd.begin (16,2);   // set up the LCD's number of columns and rows:

  //Serial.println("SensandoSignosVitales"); // prints in monitor

  //lcd.setCursor(0,0);
  //lcd.print("Inic. Medicion");  //prints in lsc screen

  // turn off leds
  digitalWrite(REDLed,LOW);
  digitalWrite(IRLed,LOW);

  for(int i=0;i<8;i++) lcd.createChar(i, sym[i]);
}

void loop ()
{  
  bool finger_status = true;
  
  float readsIR[samp_siz], sumIR,lastIR, reader, start;
  float readsRED[samp_siz], sumRED,lastRED;


  int period, samples;
  period=0; samples=0;
  int samplesCounter = 0;
  float readsIRMM[maxperiod_siz],readsREDMM[maxperiod_siz];
  int ptrMM =0;
  for (int i = 0; i < maxperiod_siz; i++) { readsIRMM[i] = 0;readsREDMM[i]=0;}
  float IRmax=0;
  float IRmin=0;
  float REDmax=0;
  float REDmin=0;
  double R=0;

  float measuresR[measures];
  int measuresPeriods[measures];
  int m = 0;
  for (int i = 0; i < measures; i++) { measuresPeriods[i]=0; measuresR[i]=0; }
   
  int ptr;

  float beforeIR;

  bool rising;
  int rise_count;
  int n;
  long int last_beat;
  for (int i = 0; i < samp_siz; i++) { readsIR[i] = 0; readsRED[i]=0; }
  sumIR = 0; sumRED=0; 
  ptr = 0; 
    
 digitalWrite(WHITELed,LOW);

  while(1)
  {
    
    //
    // turn on IR LED
    digitalWrite(REDLed,LOW);
    digitalWrite(IRLed,HIGH);
    
    // calculate an average of the sensor
    // during a 20 ms (T) period (this will eliminate
    // the 50 Hz noise caused by electric light
    n = 0;
    start = millis();
    reader = 0.;
    do
    {
      reader += analogRead (sensorPin);
      n++;
    }
    while (millis() < start + T);  
    reader /= n;  // we got an average
    // Add the newest measurement to an array
    // and subtract the oldest measurement from the array
    // to maintain a sum of last measurements
    sumIR -= readsIR[ptr];
    sumIR += reader;
    readsIR[ptr] = reader;
    lastIR = sumIR / samp_siz;

    
    //
    // TURN ON RED LED and do the same
    
    digitalWrite(REDLed,HIGH);
    digitalWrite(IRLed,LOW);

    n = 0;
    start = millis();
    reader = 0.;
    do
    {
      reader += analogRead (sensorPin);
      n++;
    }
    while (millis() < start + T);  
    reader /= n;  // we got an average
    // Add the newest measurement to an array
    // and subtract the oldest measurement from the array
    // to maintain a sum of last measurements
    sumRED -= readsRED[ptr];
    sumRED += reader;
    readsRED[ptr] = reader;
    lastRED = sumRED / samp_siz;







    //                                  
    // R CALCULATION
    // save all the samples of a period both for IR and for RED
    readsIRMM[ptrMM]=lastIR;
    readsREDMM[ptrMM]=lastRED;
    ptrMM++;
    ptrMM %= maxperiod_siz;
    samplesCounter++;
    //
    // if I've saved all the samples of a period, look to find
    // max and min values and calculate R parameter
    if(samplesCounter>=samples){
      samplesCounter =0;
      IRmax = 0; IRmin=1023; REDmax = 0; REDmin=1023;
      for(int i=0;i<maxperiod_siz;i++) {
        if( readsIRMM[i]> IRmax) IRmax = readsIRMM[i];
        if( readsIRMM[i]>0 && readsIRMM[i]< IRmin ) IRmin = readsIRMM[i];
        readsIRMM[i] =0;
        if( readsREDMM[i]> REDmax) REDmax = readsREDMM[i];
        if( readsREDMM[i]>0 && readsREDMM[i]< REDmin ) REDmin = readsREDMM[i];
        readsREDMM[i] =0;
      }
      R =  ( (REDmax-REDmin) / REDmin) / ( (IRmax-IRmin) / IRmin ) ;
    }

    

    




    // check that the finger is placed inside
    // the sensor. If the finger is missing 
    // RED curve is under the IR.
    //
    /*if (lastRED < lastIR)
    {
      if(finger_status==true)
      {
        finger_status = false;
        lcd.clear();
        lcd.setCursor(0,0);
        lcd.print("No finger?");         
      }
    }
    else
    {
      if(finger_status==false)
      {
        lcd.clear();
        finger_status = true;

        lcd.setCursor(10,0);
        lcd.print("c=");

        lcd.setCursor(0,0);
        lcd.print("bpm");
        lcd.setCursor(0,1);
        lcd.print("SpO"); lcd.print(1);  //2            
        lcd.setCursor(10,1);
        lcd.print("R=");
      }
    }*/


    float avR = 0;
    float avBPM=0;

    if (finger_status==true)
    {
          
      // lastIR holds the average of the values in the array
      // check for a rising curve (= a heart beat)
      if (lastIR > beforeIR)
      {
        rise_count++;  // count the number of samples that are rising
        if (!rising && rise_count > rise_threshold)
        {
          lcd.setCursor(3,0); 
          //lcd.print( 0 );       // <3
          // Ok, we have detected a rising curve, which implies a heartbeat.
          // Record the time since last beat, keep track of the 10 previous
          // peaks to get an average value.
          // The rising flag prevents us from detecting the same rise 
          // more than once. 
          rising = true;
      
          measuresR[m] = R;
          measuresPeriods[m] = millis() - last_beat;
          last_beat = millis();
          int period = 0;
          for(int i =0; i<measures; i++) period += measuresPeriods[i];
          
          // calculate average period and number of samples
          // to store to find min and max values
          period = period / measures;
          samples = period / (2*T);
            
          int avPeriod = 0;
          
          int c = 0;
          // c stores the number of good measures (not floating more than 10%),
          // in the last 10 peaks
          for(int i =1; i<measures; i++)
          {
            if ((measuresPeriods[i] <  measuresPeriods[i-1] * 1.1) && (measuresPeriods[i] >  measuresPeriods[i-1] / 1.1)) 
            {
              c++;
              avPeriod += measuresPeriods[i];
              avR += measuresR[i];
            }
          }
            
          m++;
          m %= measures;
                        
          lcd.setCursor(9,0);
          lcd.print("c= "+String(c)+"  ");
          
          
          // bpm and R shown are calculated as the
          // average of at least 5 good peaks
          avBPM = 60000 / ( avPeriod / c) ;
          avR = avR / c ;
          
          // if there are at last 5 measures 
          lcd.setCursor(9,1);
          if(c==0) lcd.print("R=?"); else lcd.print("R=" + String(avR) + " ");
            
          // if there are at least 5 good measures...
          if(c > 4)
          {
            digitalWrite(WHITELed,HIGH);
            // SATURTION IS A FUNCTION OF R (calibration)
            // Y = k*x + m
            // k and m are calculated with another oximeter
            float SpO2 = -19 * R + 102;
              
            lcd.setCursor(0,0);
            if(avBPM > 40 && avBPM <220)
            {
              lcd.print("         ");
              lcd.setCursor(0,0);
              lcd.print("bpm=" + String(avBPM)); //else lcd.print("---");
            }
    
            lcd.setCursor(0,1); 
            if(SpO2 > 70 && SpO2 <150) 
            {
              lcd.print("         ");
              lcd.setCursor(0,1); 
              lcd.print("SpO2=" + String(SpO2) + "%"); //else lcd.print("--% ");
            }
            digitalWrite(WHITELed,LOW);
            avR = (String(avR) == " NAN") ? 0.0 : avR;
            //Serial.print(String(avBPM)+","+String(SpO2)+","+String(avR)+","+String(c)+"\n"); 
            Serial.print(float(avBPM));
            Serial.print(","); 
            Serial.print(SpO2);
            Serial.print(","); 
            Serial.print(avR);
            Serial.print(","); 
            Serial.print(avR);
          }
          
          /*else
          {
            if(c <3)
            {
              // if less then 2 measures add ?
              lcd.setCursor(3,0); lcd.print( 2 ); //bpm ?
              lcd.setCursor(4,1); lcd.print( 2 ); //SpO2 ?
            }
          }*/
        }
      }
      else
      {
        // Ok, the curve is falling
        rising = false;
        rise_count = 0;
        //lcd.setCursor(3,0);lcd.print(" ");
      }
      
      // to compare it with the new value and find peaks
      beforeIR = lastIR;

    } // finger is inside
    
    // PLOT everything    
    /*Serial.print(lastIR);
    Serial.print(",");
    Serial.print(lastRED);*/
    /*
     * Serial.print(",");
    Serial.print(R);    
    Serial.print(",");   
    Serial.print(IRmax);
    Serial.print(",");
    Serial.print(IRmin);
    Serial.print(",");
    Serial.print(REDmax);
    Serial.print(",");
    Serial.print(REDmin);
    Serial.print(",");
    Serial.print(avR);
    Serial.print(",");
    Serial.print(avBPM); */
    //Serial.println();

    // handle the arrays      
    ptr++;
    ptr %= samp_siz;     
  } // loop while 1
}
